// Logisim project cpu.circ as structural Verilog: 1 circuit, main circuit cpu
module cpu (
  input  clk,
  input  [31:0] Instruction,
  input  [31:0] MemReadData,
  output [31:0] MemAddress,
  output [31:0] ProgramCounter,
  output [31:0] ra,
  output [31:0] sp,
  output [31:0] t0,
  output [31:0] t1,
  output [31:0] t2,
  output [31:0] s0,
  output [31:0] s1,
  output [31:0] a0,
  output [3:0] MemWriteMask,
  output [31:0] MemWriteData
);

  wire and_1_out, ASel, BrEq, BrLt, BrUn, BSel, comparator_1_eq, imm7, imm20, imm31, MemWEn, or_1_out, PCSel,
       RegWEn;
  wire [1:0] funct7_edit, WBSel;
  wire [2:0] ImmSel;
  wire [3:0] ALUSel, format, imm11_8, undriven, undriven_2, undriven_3, undriven_4, undriven_5, undriven_6,
       undriven_7, undriven_8, undriven_9, undriven_10, undriven_11, undriven_12, undriven_13, undriven_14,
       undriven_15, undriven_16, undriven_17, undriven_18, undriven_19, undriven_20, undriven_21,
       undriven_22, undriven_23;
  wire [4:0] branch_store_dest, destReg, imm11_7, multiplexer_5_out, S_format_dest, undriven_26, undriven_27,
       undriven_28, undriven_29, undriven_30, undriven_31, undriven_32, undriven_33, undriven_34;
  wire [5:0] imm30_25;
  wire [6:0] imm31_25;
  wire [7:0] imm19_12;
  wire [9:0] imm30_21;
  wire [10:0] imm31_12;
  wire [11:0] imm31_20;
  wire [31:0] B, branch_store, branched, I_imm_math, I_load, J_jal, J_jalr, no_branch,
       partial_load_1_datatoreg, partial_store_1_datatomem, PC_q, readReg1, RegWriteData, U_auipc, U_lui,
       undriven_24, undriven_25, val1, val2, val3, val6, val7, val9, val10, val11, val14, val15, val16,
       val17, val18, val19, val20, val21, val22, val23, val26, val28, val29, val30, val31;

  // Probe on PC_q
  Comparator #(.mode("unsigned"), .width(3)) comparator_1 (
    .a(ImmSel), .b(3'b010), .eq(comparator_1_eq));  // open: gt, lt
  or or_1 (or_1_out, BrEq, BrLt);
  Adder #(.width(32)) adder_1 (.a(PC_q), .b(32'h4), .out(no_branch));  // open: cin, cout
  Adder #(.width(32)) adder_2 (.a(PC_q), .b(I_imm_math), .out(branched));  // open: cin, cout
  and and_1 (and_1_out, or_1_out, comparator_1_eq);
  Register #(.width(32)) PC (.D(ProgramCounter), .en(1'b1), .clk(clk), .Q(PC_q));  // open: clr
  Multiplexer #(.enable("false"), .width(32)) multiplexer_1 (
    .in0(branched), .in1(no_branch), .out(ProgramCounter), .sel(and_1_out));
  // Probe on Instruction[24:20]
  // Probe on destReg
  // Probe on Instruction[19:15]
  // Probe on RegWriteData
  // Probe on RegWEn
  // Probe on Instruction
  // Probe on Instruction[6:2]
  // Probe on Instruction[14:12]
  // Probe on Instruction[31:25]
  // Probe on funct7_edit
  // Probe on Instruction[19:15]
  // Probe on Instruction[24:20]
  // Probe on Instruction[11:7]
  // Probe on imm31
  // Probe on imm31_25
  // Probe on imm31_12
  // Probe on imm31_20
  // Probe on imm30_25
  // Probe on imm30_21
  // Probe on imm20
  // Probe on imm19_12
  // Probe on imm11_8
  // Probe on imm11_7
  // Probe on imm7
  // Probe on ImmSel
  control_logic control_logic_1 (
    .PCSel(PCSel), .RegWEn(RegWEn), .ImmSel(ImmSel), .BrUn(BrUn), .ASel(ASel), .BSel(BSel), .ALUSel(ALUSel),
    .MemWEn(MemWEn), .WBSel(WBSel), .Instruction(Instruction), .BrEq(BrEq), .BrLt(BrLt));
  regfile regfile_1 (
    .ReadReg1(Instruction[19:15]), .ReadReg2(Instruction[24:20]), .WriteReg(destReg),
    .RegWriteData(RegWriteData), .RegWEn(RegWEn), .clk(clk), .ra(ra), .sp(sp), .t0(t0), .t1(t1), .t2(t2),
    .s0(s0), .s1(s1), .a0(a0), .RegReadData1(readReg1), .RegReadData2(branch_store));
  // Probe on branch_store
  // Probe on I_imm_math
  imm_gen imm_gen_1 (.Instruction(Instruction), .ImmSel(ImmSel), .Immediate(I_imm_math));
  // Probe on readReg1
  Multiplexer #(.enable("false"), .select(5), .width(32)) multiplexer_2 (
    .in0(I_load), .in1(val1), .in2(val2), .in3(val3), .in4(I_imm_math), .in5(U_auipc), .in6(val6),
    .in7(val7), .in8(branch_store), .in9(val9), .in10(val10), .in11(val11), .in12(branch_store),
    .in13(U_lui), .in14(val14), .in15(val15), .in16(val16), .in17(val17), .in18(val18), .in19(val19),
    .in20(val20), .in21(val21), .in22(val22), .in23(val23), .in24(branch_store), .in25(J_jalr), .in26(val26),
    .in27(J_jal), .in28(val28), .in29(val29), .in30(val30), .in31(val31), .out(B), .sel(Instruction[6:2]));
  // Probe on readReg1
  // Probe on B
  // Probe on RegWriteData
  alu alu_1 (.ALUResult(RegWriteData), .A(readReg1), .B(B), .ALUSel(ALUSel));
  // Probe on ALUSel
  branch_comp branch_comp_1 (.BrData1(readReg1), .BrData2(B), .BrUn(BrUn), .BrEq(BrEq), .BrLt(BrLt));
  Multiplexer #(.enable("false"), .select(5), .width(4)) multiplexer_3 (
    .in0(4'b0000), .in1(undriven), .in2(undriven_2), .in3(undriven_3), .in4(4'b0001), .in5(4'b0010),
    .in6(undriven_4), .in7(undriven_5), .in8(4'b0011), .in9(undriven_6), .in10(undriven_7),
    .in11(undriven_8), .in12(4'b0100), .in13(4'b0101), .in14(undriven_9), .in15(undriven_10),
    .in16(undriven_11), .in17(undriven_12), .in18(undriven_13), .in19(undriven_14), .in20(undriven_15),
    .in21(undriven_16), .in22(undriven_17), .in23(undriven_18), .in24(4'b1000), .in25(4'b0111),
    .in26(undriven_19), .in27(4'b0110), .in28(undriven_20), .in29(undriven_21), .in30(undriven_22),
    .in31(undriven_23), .out(format), .sel(Instruction[6:2]));
  // Probe on format
  // Probe on format
  // Probe on destReg
  Multiplexer #(.enable("false"), .select(4), .width(5)) multiplexer_4 (
    .in0(Instruction[11:7]), .in1(Instruction[11:7]), .in2(Instruction[11:7]), .in3(S_format_dest),
    .in4(Instruction[11:7]), .in5(Instruction[11:7]), .in6(Instruction[11:7]), .in7(Instruction[11:7]),
    .in8(branch_store_dest), .out(destReg), .sel(format));  // open: in9, in10, in11, in12, in13, in14, in15
  // Probe on multiplexer_5_out
  Multiplexer #(.enable("false"), .select(4), .width(5)) multiplexer_5 (
    .in0(undriven_26), .in1(undriven_27), .in2(undriven_28), .in3(undriven_29), .in4(undriven_30),
    .in5(undriven_31), .in6(undriven_32), .in7(undriven_33), .in8(undriven_34), .out(multiplexer_5_out),
    .sel(format));  // open: in9, in10, in11, in12, in13, in14, in15
  partial_store partial_store_1 (
    .Instruction(Instruction), .MemAddress(MemAddress), .DataFromReg(undriven_24), .MemWEn(MemWEn),
    .MemWriteMask(MemWriteMask), .DataToMem(partial_store_1_datatomem));
  partial_load partial_load_1 (
    .Instruction(Instruction), .MemAddress(MemAddress), .DataFromMem(undriven_25),
    .DataToReg(partial_load_1_datatoreg));

  // Other names for the same wires on the sheet: rs2[4:0] = Instruction[24:20]; funct7[6:0] = Instruction[31:25];
  //   funct3[2:0] = Instruction[14:12]; I_imm_math_dest[4:0] = Instruction[11:7];
  //   I_load_dest[4:0] = Instruction[11:7]; J_jal_dest[4:0] = Instruction[11:7]; J_jalr_dest[4:0] = Instruction[11:7];
  //   R_format_dest[4:0] = Instruction[11:7]; rd[4:0] = Instruction[11:7]; U_auipc_dest[4:0] = Instruction[11:7];
  //   U_lui_dest[4:0] = Instruction[11:7]; rs1[4:0] = Instruction[19:15]; opcode2_7[4:0] = Instruction[6:2];
  //   R_format[31:0] = branch_store; readReg2[31:0] = branch_store; S_format[31:0] = branch_store

  // Notes on the sheet:
  //   To IMEM
  //   IMEM (do **NOT** move this)
  //   change no-branch to ProgramCounter to undo
  //   change PC or ProgramCounter?
  //   From IMEM
  //   opcode
  //   funct3 (might have a problem being undefined)
  //   Note: funct_comb not yet defined
  //   0b0 --> 0x0
  //   only need to deal with only first and last bit
  //   0b10 = 2 --> 0x20
  //   0b01 = 1 --> 0x01
  //   Key:
  //   I-Fomat --> Load = 0
  //   U-Format auipc = 2
  //   S-Format = 3
  //   R-Format = 4
  //   U-Format lui = 5
  //   J-Formal jal = 6
  //   J-Format jalr = 7
  //   Branch / Store = 8
  //   use format to determine processing funct7 in conjunction with funct3
  //   can do addition for selection of item; use opcode as input; and output being funct_comb
  //   funct7 = 0, 0x20 (100000), or 0x01 (01) 
  //   These determine what values go to A, B
  //   Need to determine B for non I, R, S, Branch 
  //   I-Format --> imm log/arith = 1
  //   Inputs/Outputs for testing. Do **NOT** move these.
  //   It is OK to move the PC, RegFile, ALU, MEM, Branch Comp, Imm Gen, Partial Load, Partial Store and Control Logic to wherever is most convenient for you when constructing your CPU, and to delete this text
  //   might be different for lw vs. sw
  //   always a register read value
  //   either a register read value or an immediate
  //   These These determine what format to use in with less overall values
  //   Opcodes:
  //   S-Format = 8
  //   still need to put RD for S, Branch
  //   R-Format: 12
  //   Branch / Store = 24
  //   J-Format --> jal: 27; jalr: 25
  //   U-Format --> lui = 13; auipc = 5
  //   I-Type --> immediate log/arith = 4; load = 0
  //   Opcodes:
  //   R-Format: 12
  //   S-Format = 8
  //   Branch / Store = 24
  //   J-Format --> jal: 27; jalr: 25
  //   U-Format --> lui = 13; auipc = 5
  //   This row has St_B_MemWEn; comparisons for Branch (BrData1, BrData2, BrUn, BrEq, BrLt)
  //   This row has BrUn, ASel, BSel, I_format_alu, I_funct7
  //   I-Type --> immediate log/arith = 4; load = 0
  //   This row has template, MemWEn, RegWEn, WBSel, funct7_edit
  //   and R_format_alu, R_funct7
  //   These determine what the return register is
  //   still need to put RD for S, Branch
  //   This row has ImmSel, format_simp, ALUSel
  //   To DMEM
  //   [Template]
  //   ALU Key:
  //   add = 0
  //   sll = 1
  //   slt = 2
  //   srl = 5
  //   xor = 4
  //   or = 6
  //   and = 7
  //   sub = 12
  //   sra = 13
  //   S-Format = 3
  //   R-Format = 4
  //   mul (sign) = 8
  //   mulh (sign) = 9
  //   mulhu = 11
  //   bsel = 15
  //   DMEM (do **NOT** move this)
  //   Key:
  //   I-Fomat --> Load = 0
  //   I-Format --> imm log/arith = 1
  //   U-Format auipc = 2
  //   U-Format lui = 5
  //   J-Formal jal = 6
  //   J-Format jalr = 7
  //   Branch / Store = 8
  //   Key:
  //   I-Fomat --> Load = 0
  //   I-Format --> imm log/arith = 1
  //   U-Format auipc = 2
  //   S-Format = 3
  //   R-Format = 4
  //   U-Format lui = 5
  //   J-Formal jal = 6
  //   J-Format jalr = 7
  //   Branch / Store = 8
  //   From DMEM
  //   These determine
endmodule
