// Logisim project imm-gen.circ as structural Verilog: 1 circuit, main circuit imm_gen
module imm_gen (
  input  [31:0] Instruction,
  input  [2:0] ImmSel,
  output [31:0] Immediate
);

  wire [31:0] adder_1_out, bit_extender_1_out, bit_extender_2_out, bit_extender_3_out, shifter_1_out,
       shifter_2_out;

  assign bit_extender_1_out = {{28{1'b0}}, Instruction[23:20]};  // Bit_Extender bit_extender_1
  assign bit_extender_2_out = {{28{1'b0}}, Instruction[27:24]};  // Bit_Extender bit_extender_2
  assign bit_extender_3_out = {{28{1'b0}}, Instruction[31:28]};  // Bit_Extender bit_extender_3
  Shifter #(.shift("rr"), .width(32)) shifter_1 (.in(bit_extender_2_out), .\dist (5'b01000), .out(shifter_1_out));
  Shifter #(.shift("rr"), .width(32)) shifter_2 (.in(bit_extender_3_out), .\dist (5'b00100), .out(shifter_2_out));
  Adder #(.width(32)) adder_1 (.a(bit_extender_1_out), .b(shifter_1_out), .out(adder_1_out));  // open: cin, cout
  Adder #(.width(32)) adder_2 (.a(adder_1_out), .b(shifter_2_out), .out(Immediate));  // open: cin, cout

  // Notes on the sheet:
  //   INPUTS to your circuit
  //   want 31-20
  //   This circuit generates immediates
  //   DON'T CHANGE THE LOCATIONS OF THE INPUTS AND OUTPUTS!
  //   OUTPUT from your circuit
endmodule
